// Logisim project 8Bit_CPU.circ as structural Verilog: 4 circuits, main circuit main
module main (
);

  wire and_1_out, Clock_out;
  wire [7:0] undriven;

  LED led_1 (.in(Clock_out));
  Clock Clock (.out(Clock_out));
  LED led_2 (.in(and_1_out));
  buf and_1 (and_1_out, Clock_out);  // AND_Gate AND_Gate
  LED led_3 (.in(undriven[5]));
  LED led_4 (.in(undriven[4]));
  LED led_5 (.in(undriven[7]));
  LED led_6 (.in(undriven[6]));
  LED led_7 (.in(undriven[0]));
  LED led_8 (.in(undriven[1]));
  LED led_9 (.in(undriven[2]));
  LED led_10 (.in(undriven[3]));
endmodule

module SR_latch (
  input  in_1,
  input  in_2,
  output out_3,
  output out_4
);

  nor nor_1 (out_3, in_1, out_4);
  nor nor_2 (out_4, out_3, in_2);
endmodule

module Bus_Interface (
  input  Enable,
  input  Input,
  input  Input_2,
  input  Input_3,
  input  Input_4,
  input  Input_5,
  input  Input_6,
  input  Input_7,
  input  Input_8,
  output Output,
  output Output_2,
  output Output_3,
  output Output_4,
  output Output_5,
  output Output_6,
  output Output_7,
  output Output_8
);

  assign Output = Enable ? Input : 1'bz;  // Controlled_Buffer controlled_buffer_1
  assign Output_2 = Enable ? Input_2 : 1'bz;  // Controlled_Buffer controlled_buffer_2
  assign Output_3 = Enable ? Input_3 : 1'bz;  // Controlled_Buffer controlled_buffer_3
  assign Output_4 = Enable ? Input_4 : 1'bz;  // Controlled_Buffer controlled_buffer_4
  assign Output_5 = Enable ? Input_5 : 1'bz;  // Controlled_Buffer controlled_buffer_5
  assign Output_6 = Enable ? Input_6 : 1'bz;  // Controlled_Buffer controlled_buffer_6
  assign Output_7 = Enable ? Input_7 : 1'bz;  // Controlled_Buffer controlled_buffer_7
  assign Output_8 = Enable ? Input_8 : 1'bz;  // Controlled_Buffer controlled_buffer_8
endmodule

module Register (
  input  Clk,
  input  In_Enable,
  input  [7:0] Bus_In,
  input  Out_Enable,
  output [7:0] Bus_Out
);

  wire [7:0] bus_interface_1_output, register_1_q;

  Bus_Interface bus_interface_1 (
    .Enable(In_Enable), .Input(Bus_In[0]), .Input_2(Bus_In[1]), .Input_3(Bus_In[2]), .Input_4(Bus_In[3]),
    .Input_5(Bus_In[4]), .Input_6(Bus_In[5]), .Input_7(Bus_In[6]), .Input_8(Bus_In[7]),
    .Output(bus_interface_1_output[0]), .Output_2(bus_interface_1_output[1]),
    .Output_3(bus_interface_1_output[2]), .Output_4(bus_interface_1_output[3]),
    .Output_5(bus_interface_1_output[4]), .Output_6(bus_interface_1_output[5]),
    .Output_7(bus_interface_1_output[6]), .Output_8(bus_interface_1_output[7]));
  Bus_Interface bus_interface_2 (
    .Enable(Out_Enable), .Input(register_1_q[7]), .Input_2(register_1_q[6]), .Input_3(register_1_q[5]),
    .Input_4(register_1_q[4]), .Input_5(register_1_q[3]), .Input_6(register_1_q[2]),
    .Input_7(register_1_q[1]), .Input_8(register_1_q[0]), .Output(Bus_Out[7]), .Output_2(Bus_Out[6]),
    .Output_3(Bus_Out[5]), .Output_4(Bus_Out[4]), .Output_5(Bus_Out[3]), .Output_6(Bus_Out[2]),
    .Output_7(Bus_Out[1]), .Output_8(Bus_Out[0]));
  Register_part register_1 (.D(bus_interface_1_output), .en(1'b1), .Q(register_1_q), .clk(Clk), .clr(1'b0));
endmodule
